# Fritzing sketch Circuit (saved by Fritzing 0.9.5d)
breadboards: 1

parts:
  U1 = NodeMCU V1.0
  Mod1 = KY-019 5V Relay Module [package="Breakout board"]
  LED1 = smd LED [color="Red (633nm)" package="1206 [SMD]"]

nets:
  N1: U1.D2, Mod1.S
  N2: U1.GND, Mod1.-
  N3: U1.Vin, Mod1.+
  N4: Mod1.Common, LED1.cathode

notes:
  220V AC Mains
  Any Bulb

custom parts:
  NodeMCU V1.0: ESP8266 based NodeMCU
  KY-019 5V Relay Module: KY-019 5V Relay module, used to control AC circuits. (Special thanks to vanepp for fixing the PCB holes and other errors)
